# Fritzing sketch Aduino (saved by Fritzing 0.7.7b)
breadboards: 1

parts:
  Arduino1 = Arduino
  T1 = LM35 Temperature Sensor [package="TO92 [THT]"]
  R1 = Resistor [tolerance=±5% resistance=220 package=THT]
  R2 = Resistor [tolerance=±5% resistance=220 package=THT]
  Normal = Pushbutton [package="[THT]"]
  Auto/Manual = Pushbutton [package="[THT]"]
  Inversa = Pushbutton [package="[THT]"]
  R3 = Resistor [tolerance=±5% resistance=220 package=THT]
  R5 = Resistor [tolerance=±5% resistance=220 package=THT]
  R6 = Resistor [tolerance=±5% resistance=220 package=THT]
  Relé_Princ = Relay [part_number=FRS1B-S package=THT]
  Relé_Dir = Relay [part_number=FRS1B-S package=THT]
  D1 = Rectifier Diode [part_number=1N4001 package="300 mil [THT]"]
  R7 = Resistor [tolerance=±5% resistance=1k package=THT]
  R8 = Resistor [tolerance=±5% resistance=1k package=THT]
  D2 = Rectifier Diode [part_number=1N4001 package="300 mil [THT]"]
  Q1 = NPN-Transistor [package="TO92 [THT]"]
  Q2 = NPN-Transistor [package="TO92 [THT]"]
  T2 = LM35 Temperature Sensor [package="TO92 [THT]"]

nets:
  N1: Arduino1.D8, Inversa.Pin_1, Inversa.Pin_2, R6.Pin_0
  N2: Arduino1.D7, Normal.Pin_1, Normal.Pin_2, R3.Pin_0
  N3: Arduino1.D6, Auto/Manual.Pin_1, Auto/Manual.Pin_2, R5.Pin_0
  N4: Arduino1.D5, R8.Pin_0
  N5: Arduino1.D4, R7.Pin_0
  N6: Arduino1.+5V, T1.+Vs, Normal.Pin_3, Normal.Pin_4, Auto/Manual.Pin_3, Auto/Manual.Pin_4, Inversa.Pin_3, T2.+Vs
  N7: Arduino1.A1, T1.Vout, R1.Pin_0
  N8: Arduino1.A2, R2.Pin_1, T2.Vout
  GND: T1.GND, R1.Pin_1, R2.Pin_0, R5.Pin_1, Relé_Princ.COIL1, Relé_Dir.COIL1, D1.cathode, D2.cathode, Q1.E, Q2.E, T2.GND
  N9: R3.Pin_1, R6.Pin_1
  N10: Relé_Princ.C1, Relé_Princ.C2, Relé_Dir.B
  N11: Relé_Princ.COIL2, D1.anode, Q1.C
  N12: Relé_Dir.COIL2, D2.anode, Q2.C
  N13: R7.Pin_1, Q1.B
  N14: R8.Pin_1, Q2.B
